# Fritzing sketch midi_footswitch (saved by Fritzing 1.0.3b)

parts:
  Part2 = ws2812b [package="smd 2812b"]
  S3 = SWITCH-DPDT [package=os]
  Mod1 = Raspberry Pi Pico
  X1 = USB+SHIELD [package=usb-b-pth]  # not connected
  R2 = Resistor [tolerance=±5% resistance=2k package="2512 [SMD]"]
  R3 = Resistor [tolerance=±5% resistance=3k package="2512 [SMD]"]
  R4 = Resistor [tolerance=±5% resistance=5.1k package="2512 [SMD]"]
  R5 = Resistor [tolerance=±5% resistance=10k package="2512 [SMD]"]
  R6 = Resistor [tolerance=±5% resistance=30k package="2512 [SMD]"]
  S6 = Pushbutton [package=THT]
  S30 = Pushbutton [package=THT]
  S31 = Pushbutton [package=THT]
  Squix1 = OLED 0.96" 128x64 I2C SSD1306
  Part3 = ws2812b [package="smd 2812b"]
  Part4 = ws2812b [package="smd 2812b"]
  Part5 = ws2812b [package="smd 2812b"]
  Part6 = ws2812b [package="smd 2812b"]
  Part7 = ws2812b [package="smd 2812b"]
  Part8 = ws2812b [package="smd 2812b"]
  Part9 = ws2812b [package="smd 2812b"]
  Part10 = ws2812b [package="smd 2812b"]
  Part11 = ws2812b [package="smd 2812b"]
  Part12 = ws2812b [package="smd 2812b"]
  Part13 = ws2812b [package="smd 2812b"]
  Part14 = ws2812b [package="smd 2812b"]
  Part15 = ws2812b [package="smd 2812b"]
  Part16 = ws2812b [package="smd 2812b"]
  Part17 = ws2812b [package="smd 2812b"]
  R19 = Resistor [tolerance=±5% resistance=10k package="2512 [SMD]"]
  R26 = Resistor [tolerance=±5% resistance=10k package="2512 [SMD]"]
  Part19 = Adafruit HUZZAH32 ESP32 Feather [part_number="Adafruit #3405"]
  S41 = SWITCH-DPDT [package=os]
  S43 = Pushbutton [package=THT]
  S44 = SWITCH-DPDT [package=os]
  S46 = Pushbutton [package=THT]
  S47 = SWITCH-DPDT [package=os]
  S49 = Pushbutton [package=THT]
  R29 = Resistor [tolerance=±5% resistance=30k package="2512 [SMD]"]
  R30 = Resistor [tolerance=±5% resistance=10k package="2512 [SMD]"]
  R31 = Resistor [tolerance=±5% resistance=5.1k package="2512 [SMD]"]
  R32 = Resistor [tolerance=±5% resistance=3k package="2512 [SMD]"]
  R33 = Resistor [tolerance=±5% resistance=2k package="2512 [SMD]"]
  R35 = Resistor [tolerance=±5% resistance=30k package="2512 [SMD]"]
  R36 = Resistor [tolerance=±5% resistance=30k package="2512 [SMD]"]
  R37 = Resistor [tolerance=±5% resistance=10k package="2512 [SMD]"]
  R38 = Resistor [tolerance=±5% resistance=10k package="2512 [SMD]"]
  R39 = Resistor [tolerance=±5% resistance=5.1k package="2512 [SMD]"]
  R40 = Resistor [tolerance=±5% resistance=5.1k package="2512 [SMD]"]
  R41 = Resistor [tolerance=±5% resistance=3k package="2512 [SMD]"]
  R42 = Resistor [tolerance=±5% resistance=3k package="2512 [SMD]"]
  R43 = Resistor [tolerance=±5% resistance=2k package="2512 [SMD]"]
  R44 = Resistor [tolerance=±5% resistance=2k package="2512 [SMD]"]
  R46 = Resistor [tolerance=±5% resistance=10k package="2512 [SMD]"]
  R47 = Resistor [tolerance=±5% resistance=10k package="2512 [SMD]"]
  S50 = SWITCH-DPDT [package=os]
  S51 = SWITCH-DPDT [package=os]
  S52 = SWITCH-DPDT [package=os]
  S58 = Pushbutton [package=THT]
  S60 = Pushbutton [package=THT]
  S61 = Pushbutton [package=THT]
  S62 = Pushbutton [package=THT]
  S63 = SWITCH-DPDT [package=os]

nets:
  VDD: Part2.VDD, Mod1.pin_40, Squix1.VCC, Part3.VDD, Part4.VDD, Part5.VDD, Part6.VDD, Part7.VDD, Part8.VDD, Part9.VDD, Part10.VDD, Part11.VDD, Part12.VDD, Part13.VDD, Part14.VDD, Part15.VDD, Part16.VDD, Part17.VDD, Part19.VBAT
  N1: Part2.DOUT, Part3.DIN
  VSS: Part2.VSS, Mod1.pin_8, Mod1.pin_28, Mod1.pin_33, Mod1.pin_42, S6.leg1, S30.leg1, S31.leg0, Squix1.GND, Part3.VSS, Part4.VSS, Part5.VSS, Part6.VSS, Part7.VSS, Part8.VSS, Part9.VSS, Part10.VSS, Part11.VSS, Part12.VSS, Part13.VSS, Part14.VSS, Part15.VSS, Part16.VSS, Part17.VSS, Part19.GND, S43.leg1, S46.leg1, S49.leg1, S58.leg1, S60.leg1, S61.leg1, S62.leg1
  N2: Part2.DIN, Part3.DOUT, Part19.SCK
  N3: S3.2, S49.leg0
  N4: S3.3, R19.Pin_0, Part19.A3_I39
  N5: Mod1.pin_1, Part19.IO16
  N6: Mod1.pin_2, Part19.IO17
  N7: R2.Pin_0, R3.Pin_1, S41.1
  N8: R2.Pin_1, R26.Pin_0, Part19.A4_IO36
  N9: R3.Pin_0, R4.Pin_1, S44.1
  N10: R4.Pin_0, R5.Pin_1, S47.1
  N11: R5.Pin_0, R6.Pin_1
  N12: R6.Pin_0, S30.leg0
  N13: S6.leg0, S47.2
  N14: S31.leg1, R35.Pin_0
  N15: Squix1.SCL, Part19.SCL
  N16: Squix1.SCA, Part19.SDA
  N17: Part4.DOUT, Part5.DIN
  N18: Part4.DIN, Part5.DOUT
  N19: Part6.DOUT, Part7.DIN
  N20: Part6.DIN, Part7.DOUT
  N21: Part8.DOUT, Part9.DIN
  N22: Part8.DIN, Part9.DOUT
  N23: Part10.DOUT, Part11.DIN
  N24: Part10.DIN, Part11.DOUT
  N25: Part12.DOUT, Part13.DIN
  N26: Part12.DIN, Part13.DOUT
  N27: Part14.DOUT, Part15.DIN
  N28: Part14.DIN, Part15.DOUT
  N29: Part16.DOUT, Part17.DIN
  N30: Part16.DIN, Part17.DOUT
  N31: R19.Pin_1, R26.Pin_1
  N32: Part19.A2_I34, R43.Pin_1, R47.Pin_0, S63.1
  N33: Part19.3.3V, R46.Pin_1, R47.Pin_1
  N34: Part19.IO32_A7, R46.Pin_0, S63.3
  N35: S41.2, S43.leg0
  N36: S41.3, R32.Pin_1, R33.Pin_0
  N37: S44.2, S46.leg0
  N38: S44.3, R31.Pin_1, R32.Pin_0
  N39: S47.3, R30.Pin_1, R31.Pin_0
  N40: R29.Pin_1, R30.Pin_0
  N41: R35.Pin_1, R37.Pin_0
  N42: R36.Pin_1, R38.Pin_0
  N43: R37.Pin_1, S52.1
  N44: R38.Pin_1, R40.Pin_0, S52.3
  N45: R39.Pin_1, R41.Pin_0, S51.1
  N46: R40.Pin_1, R42.Pin_0, S51.2, S51.3, S58.leg0
  N47: R41.Pin_1, R43.Pin_0, S50.1
  N48: R42.Pin_1, R44.Pin_0, S50.3
  N49: S50.2, S60.leg0
  N50: S52.2, S61.leg0
  N51: S62.leg0, S63.2

notes:
  Pedal 1 - Momentary
  Pedal 2 - Latch Emulation
  Pedal 3 - Momentary
  Pedal 5 - Latch Emulation
  Pedal 6 - To Extra Connector
  - Ring
  - Tip
  - Sleeve

custom parts:
  Raspberry Pi Pico: Raspberry Pi Pico. Based around the RP2040 microcontroller the Pico is a low cost microcontroller device bringing Raspberry Pi quality, cost, and easy of use to the microcontroller space. Jan 2021, Split part in to two versions: tht (this one) and SMD. This one will drill holes for a .1 in header in pcb to allow plugging in the module as well as providing pads to solder the module to the top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
